# Fritzing sketch Halloween 2016 (saved by Fritzing 0.9.3b)

parts:
  Part1 = Audio FX Sound Board
  Part2 = Arduino Uno (Rev3)
  R1 = Resistor [tolerance=±5% resistance=220 package=THT]
  R2 = Resistor [tolerance=±5% resistance=220 package=THT]
  R3 = Resistor [tolerance=±5% resistance=220 package=THT]
  R4 = Resistor [tolerance=±5% resistance=220 package=THT]
  LED1 = LED - 5mm [color="Red (633nm)" package="5 mm [THT]"]
  LED2 = LED - 5mm [color="Red (633nm)" package="5 mm [THT]"]
  LED3 = LED - 5mm [color="White (6500K)" package="5 mm [THT]"]
  LED4 = LED - 5mm [color="White (6500K)" package="5 mm [THT]"]

nets:
  VIN: Part1.VIN, Part2.5V
  GND: Part1.GND, Part2.GND, LED1.cathode, LED2.cathode, LED3.cathode, LED4.cathode
  N1: Part2.D2, R3.Pin_0, R4.Pin_0
  N2: Part2.D3_PWM, R1.Pin_1, R2.Pin_1
  N3: R1.Pin_0, LED1.anode
  N4: R2.Pin_0, LED2.anode
  N5: R3.Pin_1, LED3.anode
  N6: R4.Pin_1, LED4.anode

custom parts:
  Audio FX Sound Board: The Adafruit Sound Board, the fastest way to add audio effects to a project!
